# Fritzing sketch Fade (saved by Fritzing 0.9.3b)
breadboards: 1

parts:
  Arduino = Arduino Uno (Rev3)
  R1 = Resistor [tolerance=±5% resistance=1k package=THT]
  R2 = Resistor [tolerance=±5% resistance=1k package=THT]
  R3 = Resistor [tolerance=±5% resistance=1k package=THT]
  LED1 = LED - 5mm [color="Red (633nm)" package="5 mm [THT]"]
  S1 = Pushbutton [package="[THT]"]
  S2 = Pushbutton [package="[THT]"]

nets:
  GND: Arduino.GND, LED1.cathode, S1.Pin_1, S1.Pin_2, S2.Pin_1, S2.Pin_2
  N1: Arduino.D2, R1.Pin_0, S1.Pin_3, S1.Pin_4
  N2: Arduino.D3_PWM, R2.Pin_0, S2.Pin_3, S2.Pin_4
  N3: Arduino.D5_PWM, R3.Pin_0
  N4: Arduino.5V, R1.Pin_1, R2.Pin_1
  N5: R3.Pin_1, LED1.anode
