# Fritzing sketch Esquema Serial TX RX (saved by Fritzing 0.9.3b)
breadboards: 1

parts:
  Arduino = Arduino Uno (Rev3)
  R1 = Resistor [tolerance=±5% resistance=1k package=THT]
  S1 = Pushbutton [package="[THT]"]
  R2 = Resistor [tolerance=±5% resistance=1k package=THT]
  LED1 = LED - 5mm [color="Red (633nm)" package="5 mm [THT]"]

nets:
  N1: Arduino.D10_PWM/SS, R1.Pin_0, S1.Pin_1, S1.Pin_2
  N2: Arduino.D7, R2.Pin_0
  N3: Arduino.5V, R1.Pin_1
  N4: Arduino.GND, S1.Pin_3, S1.Pin_4, LED1.cathode
  N5: R2.Pin_1, LED1.anode
