# Fritzing sketch Esquema Circuito RC (saved by Fritzing 0.9.3b)
breadboards: 1

parts:
  Arduino = Arduino Uno (Rev3)
  R1 = Resistor [tolerance=±5% resistance=1k package=THT]
  C1 = Electrolytic Capacitor [capacitance=100µF package="100 mil [THT, electrolytic]"]

nets:
  N1: Arduino.A0, R1.Pin_1, C1.+
  N2: Arduino.D10_PWM/SS, R1.Pin_0
  GND: Arduino.GND, C1.-
