# Fritzing sketch Servo (saved by Fritzing 0.9.3b)
breadboards: 1

parts:
  Arduino = Arduino Uno (Rev3)
  Microservo_9g = Basic Servo
  R1 = Slide Potentiometer [maximum_resistance=10kΩ]

nets:
  N1: Arduino.A0, R1.wiper
  N2: Arduino.D9_PWM, Microservo_9g.pulse
  GND: Arduino.GND, Microservo_9g.gnd, R1.leg1
  5V: Arduino.5V, Microservo_9g.vcc, R1.leg2
