# Fritzing sketch Esquema Braco Robotico (saved by Fritzing 0.9.3b)
breadboards: 1

parts:
  Arduino_Uno = Arduino Uno (Rev3)
  Micro_servo_9g = Basic Servo [part_number=Rotação]
  Micro_servo_9g_2 = Basic Servo [part_number=Altura]
  Micro_servo_9g_3 = Basic Servo [part_number=Profundidade]
  Micro_servo_9g_4 = Basic Servo [part_number=Cabeça]
  R1 = Slide Potentiometer [maximum_resistance=10kΩ part_number=Profundidade]
  R2 = Slide Potentiometer [maximum_resistance=10kΩ part_number=Cabeça]
  R3 = Slide Potentiometer [maximum_resistance=10kΩ part_number=Rotação]
  R4 = Slide Potentiometer [maximum_resistance=10kΩ part_number=Altura]

nets:
  N1: Arduino_Uno.A0, R2.wiper
  N2: Arduino_Uno.A1, R1.wiper
  N3: Arduino_Uno.A2, R4.wiper
  N4: Arduino_Uno.A3, R3.wiper
  N5: Arduino_Uno.D9_PWM, Micro_servo_9g_3.pulse
  N6: Arduino_Uno.D11_PWM/MOSI, Micro_servo_9g_4.pulse
  GND: Arduino_Uno.GND, Micro_servo_9g.gnd, Micro_servo_9g_2.gnd, Micro_servo_9g_3.gnd, Micro_servo_9g_4.gnd, R1.leg1, R2.leg1, R3.leg1, R4.leg1
  N7: Arduino_Uno.D3_PWM, Micro_servo_9g.pulse
  N8: Arduino_Uno.D5_PWM, Micro_servo_9g_2.pulse
  5V: Arduino_Uno.5V, Micro_servo_9g.vcc, Micro_servo_9g_2.vcc, Micro_servo_9g_3.vcc, Micro_servo_9g_4.vcc
  N9: R1.leg2, R2.leg2
  N10: R3.leg2, R4.leg2
