# Fritzing sketch EsquemaJogoLeds (saved by Fritzing 0.9.3b)
breadboards: 1

parts:
  Componente1 = Arduino Nano (Rev3.0)
  R1 = Resistor [tolerance=±5% resistance=1k package=THT]
  R2 = Resistor [tolerance=±5% resistance=1k package=THT]
  R3 = Resistor [tolerance=±5% resistance=1k package=THT]
  R4 = Resistor [tolerance=±5% resistance=1k package=THT]
  R5 = Resistor [tolerance=±5% resistance=1k package=THT]
  R6 = Resistor [tolerance=±5% resistance=1k package=THT]
  LED = LED - 5mm [color="Red (633nm)" package="5 mm [THT]"]
  LED2 = LED - 5mm [color="Red (633nm)" package="5 mm [THT]"]
  LED3 = LED - 5mm [color="Red (633nm)" package="5 mm [THT]"]
  R7 = Resistor [tolerance=±5% resistance=1k package=THT]
  R8 = Resistor [tolerance=±5% resistance=1k package=THT]
  Resistores = Resistor [tolerance=±5% resistance=1k package=THT]
  R10 = Resistor [tolerance=±5% resistance=1k package=THT]
  LED4 = LED - 5mm [color="Red (633nm)" package="5 mm [THT]"]
  LED5 = LED - 5mm [color="Red (633nm)" package="5 mm [THT]"]
  LED6 = LED - 5mm [color="Red (633nm)" package="5 mm [THT]"]
  LED7 = LED - 5mm [color="Red (633nm)" package="5 mm [THT]"]
  LED8 = LED - 5mm [color="Red (633nm)" package="5 mm [THT]"]
  LED9 = LED - 5mm [color="Red (633nm)" package="5 mm [THT]"]
  LED10 = LED - 5mm [color="Red (633nm)" package="5 mm [THT]"]

nets:
  N1: Componente1.GND, LED.cathode, LED2.cathode, LED3.cathode, LED4.cathode, LED5.cathode, LED6.cathode, LED7.cathode, LED8.cathode, LED9.cathode, LED10.cathode
  N2: Componente1.D2, R10.Pin_0
  N3: Componente1.D3, R1.Pin_0
  N4: Componente1.D4, R2.Pin_0
  N5: Componente1.D5, R3.Pin_0
  N6: Componente1.D6, R4.Pin_0
  N7: Componente1.D7, R5.Pin_0
  N8: Componente1.D8, R6.Pin_0
  N9: Componente1.D9, R7.Pin_0
  N10: Componente1.D10, R8.Pin_0
  N11: Componente1.D11/MOSI, Resistores.Pin_0
  N12: R1.Pin_1, LED9.anode
  N13: R2.Pin_1, LED8.anode
  N14: R3.Pin_1, LED7.anode
  N15: R4.Pin_1, LED6.anode
  N16: R5.Pin_1, LED5.anode
  N17: R6.Pin_1, LED4.anode
  N18: LED.anode, Resistores.Pin_1
  N19: LED2.anode, R8.Pin_1
  N20: LED3.anode, R7.Pin_1
  N21: R10.Pin_1, LED10.anode
